# Fritzing sketch sketch (saved by Fritzing 0.9.2b)
breadboards: 1

parts:
  Part1 = Arduino Uno (Rev3)
  Part2 = Bluetooth HC-05 Macho
  T1 = LM35 Temperature Sensor [package="TO92 [THT]"]
  LED1 = LED - 3mm [color="Red (633nm)" package="3 mm [THT]"]
  R1 = Resistor [tolerance=±5% resistance=220 package=THT]

nets:
  N1: Part1.A0, T1.Vout
  N2: Part1.D12/MISO, R1.Pin_0
  GND: Part1.GND, Part2.GND, T1.GND, LED1.cathode
  N3: Part1.D0/RX, Part2.TXD
  N4: Part1.D1/TX, Part2.RXD
  5V: Part1.5V, Part2.VCC, T1.+Vs
  N5: LED1.anode, R1.Pin_1
